# Fritzing sketch CylonBoard (saved by Fritzing 0.9.1b)
circuit board: 13.4046cm x 8.76044cm
breadboards: 1
stripboards: 2

parts:
  Left_Engine = NPN-Transistor [package="TO92 [THT]"]
  R2 = Resistor [tolerance=±5% resistance=470 package=THT]
  R3 = Resistor [tolerance=±5% resistance=470 package=THT]
  R4 = Resistor [tolerance=±5% resistance=470 package=THT]
  R5 = Resistor [tolerance=±5% resistance=470 package=THT]
  R6 = Resistor [tolerance=±5% resistance=470 package=THT]
  R8 = Resistor [tolerance=±5% resistance=470 package=THT]
  S3 = Pushbutton [package=THT]
  R9 = Resistor [tolerance=±5% resistance=470 package=THT]
  TIP124 = NPN-Transistor [package="TO92 [THT]"]
  Pad94 = Pad [width=2.76739585405409 height=2.95847939376991 connect=center]
  Pad95 = Pad [width=2.76739585405409 height=2.95847939376991 connect=center]
  Pad93 = Pad [width=2.76739585405409 height=2.95847939376991 connect=center]
  Pad91 = Pad [width=2.76739585405409 height=2.95847939376991 connect=center]
  Pad92 = Pad [width=2.76739585405409 height=2.95847939376991 connect=center]
  Pad96 = Pad [width=2.76739585405409 height=2.95847939376991 connect=center]
  Pad101 = Pad [width=2.76739585405409 height=2.95847939376991 connect=center]
  Pad90 = Pad [width=2.76739585405409 height=2.95847939376991 connect=center]
  Pad100 = Pad [width=2.76739585405409 height=2.95847939376991 connect=center]
  Pad98 = Pad [width=2.76739585405409 height=2.95847939376991 connect=center]
  Pad97 = Pad [width=2.76739585405409 height=2.95847939376991 connect=center]
  Pad99 = Pad [width=2.76739585405409 height=2.95847939376991 connect=center]
  Pad82 = Pad [width=2.76739585405409 height=2.95847939376991 connect=center]
  Pad81 = Pad [width=2.76739585405409 height=2.95847939376991 connect=center]
  Pad89 = Pad [width=2.76739585405409 height=2.95847939376991 connect=center]
  Pad80 = Pad [width=2.76739585405409 height=2.95847939376991 connect=center]
  Pad78 = Pad [width=2.76739585405409 height=2.95847939376991 connect=center]
  Pad77 = Pad [width=2.76739585405409 height=2.95847939376991 connect=center]
  Pad79 = Pad [width=2.76739585405409 height=2.95847939376991 connect=center]
  Pad102 = Pad [width=2.76739585405409 height=2.95847939376991 connect=center]
  Pad88 = Pad [width=2.76739585405409 height=2.95847939376991 connect=center]
  Pad83 = Pad [width=2.76739585405409 height=2.95847939376991 connect=center]
  Pad87 = Pad [width=2.76739585405409 height=2.95847939376991 connect=center]
  Pad85 = Pad [width=2.76739585405409 height=2.95847939376991 connect=center]
  Pad84 = Pad [width=2.76739585405409 height=2.95847939376991 connect=center]
  Pad86 = Pad [width=2.76739585405409 height=2.95847939376991 connect=center]
  Pad103 = Pad [width=2.76739585405409 height=2.95847939376991 connect=center]
  Pad104 = Pad [width=2.76739585405409 height=2.95847939376991 connect=center]
  Pad76 = Pad [width=2.76739585405409 height=2.95847939376991 connect=center]
  Pad27 = Pad [width=2.76739585405409 height=2.95847939376991 connect=center]
  Pad34 = Pad [width=2.76739585405409 height=2.95847939376991 connect=center]
  Pad75 = Pad [width=2.76739585405409 height=2.95847939376991 connect=center]
  Pad33 = Pad [width=2.76739585405409 height=2.95847939376991 connect=center]
  Pad31 = Pad [width=2.76739585405409 height=2.95847939376991 connect=center]
  Pad32 = Pad [width=2.76739585405409 height=2.95847939376991 connect=center]
  Pad35 = Pad [width=2.76739585405409 height=2.95847939376991 connect=center]
  Pad41 = Pad [width=2.76739585405409 height=2.95847939376991 connect=center]
  Pad36 = Pad [width=2.76739585405409 height=2.95847939376991 connect=center]
  Pad40 = Pad [width=2.76739585405409 height=2.95847939376991 connect=center]
  Pad38 = Pad [width=2.76739585405409 height=2.95847939376991 connect=center]
  Pad37 = Pad [width=2.76739585405409 height=2.95847939376991 connect=center]
  Pad39 = Pad [width=2.76739585405409 height=2.95847939376991 connect=center]
  Pad30 = Pad [width=2.76739585405409 height=2.95847939376991 connect=center]
  Pad21 = Pad [width=2.76739585405409 height=2.95847939376991 connect=center]
  Pad29 = Pad [width=2.76739585405409 height=2.95847939376991 connect=center]
  Pad20 = Pad [width=2.76739585405409 height=2.95847939376991 connect=center]
  Pad18 = Pad [width=2.76739585405409 height=2.95847939376991 connect=center]
  Pad17 = Pad [width=2.76739585405409 height=2.95847939376991 connect=center]
  Pad19 = Pad [width=2.76739585405409 height=2.95847939376991 connect=center]
  Pad22 = Pad [width=2.76739585405409 height=2.95847939376991 connect=center]
  Pad28 = Pad [width=2.76739585405409 height=2.95847939376991 connect=center]
  Pad23 = Pad [width=2.76739585405409 height=2.95847939376991 connect=center]
  Pad25 = Pad [width=2.76739585405409 height=2.95847939376991 connect=center]
  Pad24 = Pad [width=2.76739585405409 height=2.95847939376991 connect=center]
  Pad26 = Pad [width=2.76739585405409 height=2.95847939376991 connect=center]
  Pad42 = Pad [width=2.76739585405409 height=2.95847939376991 connect=center]
  Pad67 = Pad [width=2.76739585405409 height=2.95847939376991 connect=center]
  Pad43 = Pad [width=2.76739585405409 height=2.95847939376991 connect=center]
  Pad66 = Pad [width=2.76739585405409 height=2.95847939376991 connect=center]
  Pad64 = Pad [width=2.76739585405409 height=2.95847939376991 connect=center]
  Pad65 = Pad [width=2.76739585405409 height=2.95847939376991 connect=center]
  Pad68 = Pad [width=2.76739585405409 height=2.95847939376991 connect=center]
  Pad74 = Pad [width=2.76739585405409 height=2.95847939376991 connect=center]
  Pad69 = Pad [width=2.76739585405409 height=2.95847939376991 connect=center]
  Pad73 = Pad [width=2.76739585405409 height=2.95847939376991 connect=center]
  Pad71 = Pad [width=2.76739585405409 height=2.95847939376991 connect=center]
  Pad70 = Pad [width=2.76739585405409 height=2.95847939376991 connect=center]
  Pad72 = Pad [width=2.76739585405409 height=2.95847939376991 connect=center]
  Pad63 = Pad [width=2.76739585405409 height=2.95847939376991 connect=center]
  Pad48 = Pad [width=2.76739585405409 height=2.95847939376991 connect=center]
  Pad62 = Pad [width=2.76739585405409 height=2.95847939376991 connect=center]
  Pad47 = Pad [width=2.76739585405409 height=2.95847939376991 connect=center]
  Pad45 = Pad [width=2.76739585405409 height=2.95847939376991 connect=center]
  Pad44 = Pad [width=2.76739585405409 height=2.95847939376991 connect=center]
  Pad46 = Pad [width=2.76739585405409 height=2.95847939376991 connect=center]
  Pad49 = Pad [width=2.76739585405409 height=2.95847939376991 connect=center]
  Pad61 = Pad [width=2.76739585405409 height=2.95847939376991 connect=center]
  Pad50 = Pad [width=2.76739585405409 height=2.95847939376991 connect=center]
  Pad58 = Pad [width=2.76739585405409 height=2.95847939376991 connect=center]
  Pad53 = Pad [width=2.76739585405409 height=2.95847939376991 connect=center]
  Pad52 = Pad [width=2.76739585405409 height=2.95847939376991 connect=center]
  Pad54 = Pad [width=2.76739585405409 height=2.95847939376991 connect=center]
  Pad105 = Pad [width=2.76739585405409 height=2.95847939376991 connect=center]
  Digispark2 = Digispark
  Power_plug2 = Power plug
  R1 = Resistor [tolerance=±5% resistance=470 package=THT]
  TIP125 = NPN-Transistor [package="TO92 [THT]"]
  TIP126 = NPN-Transistor [package="TO92 [THT]"]
  R25 = Resistor [tolerance=±5% resistance=470 package=THT]
  R26 = Resistor [tolerance=±5% resistance=470 package=THT]
  R27 = Resistor [tolerance=±5% resistance=470 package=THT]
  R28 = Resistor [tolerance=±5% resistance=470 package=THT]
  R29 = Resistor [tolerance=±5% resistance=470 package=THT]
  R30 = Resistor [tolerance=±5% resistance=470 package=THT]
  TIP127 = NPN-Transistor [package="TO92 [THT]"]
  R35 = Resistor [tolerance=±5% resistance=470 package=THT]
  R36 = Resistor [tolerance=±5% resistance=470 package=THT]
  R37 = Resistor [tolerance=±5% resistance=470 package=THT]
  R38 = Resistor [tolerance=±5% resistance=470 package=THT]
  J1 = Screw terminal - 2 pins [package=THT]
  J2 = Screw terminal - 2 pins [package=THT]
  J3 = Screw terminal - 2 pins [package=THT]
  J4 = Screw terminal - 2 pins [package=THT]
  J5 = Screw terminal - 2 pins [package=THT]
  J6 = Screw terminal - 2 pins [package=THT]
  J7 = Screw terminal - 2 pins [package=THT]
  J8 = Screw terminal - 2 pins [package=THT]
  J9 = Screw terminal - 2 pins [package=THT]
  J10 = Screw terminal - 2 pins [package=THT]
  J11 = Screw terminal - 2 pins [package=THT]
  J12 = Screw terminal - 2 pins [package=THT]
  J13 = Screw terminal - 2 pins [package=THT]
  J14 = Screw terminal - 2 pins [package=THT]
  J15 = Screw terminal - 2 pins [package=THT]
  J16 = Screw terminal - 2 pins [package=THT]
  J17 = Screw terminal - 2 pins [package=THT]
  J18 = Screw terminal - 2 pins [package=THT]
  LED1 = LED - 5mm [color="Red (633nm)" package="5 mm [THT]"]

nets:
  N1: Left_Engine.E, Digispark2.P5
  VIN: Left_Engine.B, TIP124.B, Digispark2.VIN, Power_plug2.VCC, TIP125.B, TIP126.B, TIP127.B
  N2: Left_Engine.C, R29.Pin_1, R30.Pin_1
  N3: R2.Pin_0, J4.pin2, LED1.anode
  N4: R2.Pin_1, R3.Pin_1, R8.Pin_1, R1.Pin_1, TIP126.C
  N5: R3.Pin_0, J5.pin2
  N6: R4.Pin_0, J11.pin2
  N7: R4.Pin_1, R5.Pin_1, R6.Pin_1, R9.Pin_1, R25.Pin_1, R26.Pin_1, R27.Pin_1, R28.Pin_1, TIP127.C
  N8: R5.Pin_0, J16.pin2
  N9: R6.Pin_0, J18.pin2
  N10: R8.Pin_0, J6.pin2
  N11: S3.leg0, Digispark2.GND, J1.pin1, J2.pin1, J3.pin1, J4.pin1, J5.pin1, J6.pin1, J7.pin1, J8.pin1, J9.pin1, J10.pin1, J11.pin1, J12.pin1, J13.pin1, J14.pin1, J15.pin1, J16.pin1, J17.pin1, J18.pin1, LED1.cathode
  N12: S3.leg1, Power_plug2.GND
  N13: R9.Pin_0, J17.pin2
  N14: TIP124.E, Digispark2.P4
  N15: TIP124.C, R37.Pin_1, R38.Pin_1
  N16: Pad94.pad, Pad95.pad, Pad93.pad, Pad91.pad, Pad92.pad, Pad96.pad, Pad101.pad, Pad90.pad, Pad100.pad, Pad98.pad, Pad97.pad, Pad99.pad, Pad82.pad, Pad81.pad, Pad89.pad, Pad80.pad, Pad78.pad, Pad77.pad, Pad79.pad, Pad102.pad, Pad88.pad, Pad83.pad, Pad87.pad, Pad85.pad, Pad84.pad, Pad86.pad, Pad103.pad, Pad104.pad, Pad76.pad, Pad75.pad, Pad67.pad, Pad66.pad, Pad64.pad, Pad65.pad, Pad68.pad, Pad74.pad, Pad69.pad, Pad73.pad, Pad71.pad, Pad70.pad, Pad72.pad
  N17: Pad27.pad, Pad34.pad, Pad33.pad, Pad31.pad, Pad32.pad, Pad35.pad, Pad41.pad, Pad36.pad, Pad40.pad, Pad38.pad, Pad37.pad, Pad39.pad, Pad30.pad, Pad21.pad, Pad29.pad, Pad20.pad, Pad18.pad, Pad17.pad, Pad19.pad, Pad22.pad, Pad28.pad, Pad23.pad, Pad25.pad, Pad24.pad, Pad26.pad, Pad42.pad, Pad43.pad, Pad63.pad, Pad48.pad, Pad62.pad, Pad47.pad, Pad45.pad, Pad44.pad, Pad46.pad, Pad49.pad, Pad61.pad, Pad50.pad, Pad58.pad, Pad53.pad, Pad52.pad, Pad54.pad, Pad105.pad
  N18: Digispark2.P0, TIP127.E
  N19: Digispark2.P1, TIP126.E
  N20: Digispark2.P2, TIP125.E
  N21: R1.Pin_0, J3.pin2
  N22: TIP125.C, R35.Pin_1, R36.Pin_1
  N23: R25.Pin_0, J14.pin2
  N24: R26.Pin_0, J12.pin2
  N25: R27.Pin_0, J15.pin2
  N26: R28.Pin_0, J10.pin2
  N27: R29.Pin_0, J2.pin2
  N28: R30.Pin_0, J1.pin2
  N29: R35.Pin_0, J13.pin2
  N30: R36.Pin_0, J9.pin2
  N31: R37.Pin_0, J7.pin2
  N32: R38.Pin_0, J8.pin2

notes:
  Guns
  Engines
  Spot
  Cockpit
  Spotlights
  Headlights
  Screwdown Terminals for runs to LEDs.

custom parts:
  Digispark: The Digispark is an Attiny85 based microcontroller development board similar to the Arduino line, only cheaper, smaller, and a bit less powerful. With a whole host of shields to extend its functionality and the ability to use the familiar Arduino IDE the Digispark is a great way to jump into electronics, or perfect for when an Arduino is too big or too much.
